# Fritzing sketch node-hardware (saved by Fritzing 0.9.3b)

parts:
  A1 = Renke rs485 soil ph-sensor
  A2 = Soil Moisture Detection Module
  A4 = DORHEA ESP32 GPIO breakout board 30pin
  M1 = DOIT Esp32 DevKit v1 (30 pins long, 11 pins width) [part_number=ESP32S-PIN30]  # not connected
  U1 = MAX485 Breakout [chip_label=? package=THT]
  JACK1 = 2.1mm Barrel Jack with Terminal Block

nets:
  N1: A1.Pin_1, U1.B
  N2: A1.Pin_2, U1.A
  N3: A1.Pin_3, JACK1.POS
  GND: A1.Pin_4, A2.GND, A4.Pin_36, A4.Pin_55, A4.Pin_56, A4.Pin_57, U1.GND, JACK1.NEG
  N4: A2.AO, A4.Pin_4, A4.Pin_43
  N5: A2.VCC, A4.Pin_61, A4.Pin_62
  N6: A4.Pin_59, U1.VCC
  N7: A4.Pin_72, A4.Pin_119, U1.DI
  N8: A4.Pin_117, U1.RE, U1.DE
  N9: A4.Pin_118, U1.RO

notes:
  soil moisture sensor
  12V power adapter
  esp32

custom parts:
  Renke rs485 soil ph-sensor: The soil pH sensor is a device that measures the current pH of the soil. It detects the pH value of the soil by inserting two stainless steel probes vertically into the soil.
  DORHEA ESP32 GPIO breakout board 30pin: ESP32 shield 30P expansion board, supports two power supply : DC 6.5-16v and USB 5.V
  DOIT Esp32 DevKit v1 (30 pins long, 11 pins width): The DOIT Esp32 DevKit v1 is one of the development board created by DOIT to evaluate the ESP-WROOM-32 module. It is based on the ESP32 microcontroller that boasts Wifi, Bluetooth, Ethernet and Low Power support all in a single chip. (vanepp) made breadboard work, adjusted pin numbering and labels and reduced size of schematic and cleaned up pcb. This chip is 30pins long (2 x15) and 11 pins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
  MAX485 Breakout: MAX485 RS485 breakout board
